// Logisim project uart - Copy.circ as structural Verilog: 6 circuits, main circuit main
module main (
);

  uart uart_1 ();  // open: baudsel, clk, cycle, rxbit, cts, reset, rts, dout, din, error, done, done_2, txbit
endmodule

module baud (
  input  [2:0] baud,
  input  clk,
  input  reset,
  input  clr_clk,
  output baud_clock
);

  wire and_1_out, comparator_1_eq, d_ff_1_q, d_ff_2_q, multiplexer_4_out, multiplexer_5_out;
  wire [3:0] adder_2_out, multiplexer_2_out, multiplexer_6_out, register_2_q;
  wire [11:0] adder_1_out, multiplexer_1_out, multiplexer_3_out, register_1_q;

  Multiplexer #(.select(3), .width(12), .enable("false")) multiplexer_1 (
    .in0(12'h7), .in1(12'hf), .in2(12'h17), .in3(12'h2f), .in4(12'h5f), .in5(12'hbf), .in6(12'h17f),
    .in7(12'h2ff), .out(multiplexer_1_out), .sel(baud));
  Adder #(.width(12)) adder_1 (.a(register_1_q), .b(12'h1), .out(adder_1_out));  // open: cin, cout
  Comparator #(.width(12), .mode("unsigned")) comparator_1 (
    .a(multiplexer_1_out), .b(register_1_q), .eq(comparator_1_eq));  // open: gt, lt
  Multiplexer #(.width(4), .enable("false")) multiplexer_2 (
    .in0(register_2_q), .in1(adder_2_out), .out(multiplexer_2_out), .sel(d_ff_1_q));
  Adder #(.width(4)) adder_2 (.a(register_2_q), .b(4'b0001), .out(adder_2_out));  // open: cin, cout
  and and_1 (and_1_out, ~d_ff_2_q, clr_clk);  // AND_Gate
  Register #(.width(12)) register_1 (.D(multiplexer_3_out), .clk(clk), .Q(register_1_q), .clr(reset));  // open: en
  Multiplexer #(.width(12), .enable("false")) multiplexer_3 (
    .in0(adder_1_out), .in1({12{1'b0}}), .out(multiplexer_3_out), .sel(comparator_1_eq));
  D_Flip_Flop d_ff_1 (.D(multiplexer_4_out), .clk(clk), .Q(d_ff_1_q), .reset(reset));  // open: Qn, preset
  Multiplexer #(.enable("false")) multiplexer_4 (
    .in0(1'b0), .in1(1'b1), .out(multiplexer_4_out), .sel(comparator_1_eq));
  D_Flip_Flop d_ff_2 (.D(multiplexer_5_out), .clk(clk), .Q(d_ff_2_q), .reset(reset));  // open: Qn, preset
  Multiplexer #(.enable("false")) multiplexer_5 (.in0(1'b0), .in1(1'b1), .out(multiplexer_5_out), .sel(clr_clk));
  Register #(.width(4)) register_2 (.D(multiplexer_6_out), .clk(clk), .Q(register_2_q), .clr(reset));  // open: en
  Multiplexer #(.width(4), .enable("false")) multiplexer_6 (
    .in0(multiplexer_2_out), .in1(4'b1000), .out(multiplexer_6_out), .sel(and_1_out));
  Comparator #(.width(4), .mode("unsigned")) comparator_2 (
    .a(register_2_q), .b(4'b1111), .eq(baud_clock));  // open: gt, lt
endmodule

module transmit (
  input  rts,
  input  stop,
  input  [15:0] dout,
  input  reset,
  input  baud_clock,
  output sent_ok,
  output txbit
);

  wire and_1_out, comparator_1_eq, comparator_2_eq, comparator_3_eq, comparator_4_eq, comparator_5_eq,
       comparator_6_eq, d_ff_2_q, multiplexer_7_out, multiplexer_11_out, multiplexer_12_out, or_1_out;
  wire [1:0] multiplexer_1_out, multiplexer_2_out, multiplexer_3_out, multiplexer_4_out, multiplexer_6_out,
       register_1_q;
  wire [1:1] parity_1_paritybit;
  wire [7:0] adder_1_out, multiplexer_9_out, multiplexer_10_out, register_3_q;
  wire [18:0] multiplexer_5_out, multiplexer_8_out, register_2_q;

  Comparator comparator_1 (.a(8'h12), .b(register_3_q), .eq(comparator_1_eq));  // open: gt, lt
  and and_1 (and_1_out, rts, comparator_2_eq);
  Comparator #(.width(2), .mode("unsigned")) comparator_2 (
    .a(register_1_q), .b(2'b00), .eq(comparator_2_eq));  // open: gt, lt
  Comparator #(.width(2), .mode("unsigned")) comparator_3 (
    .a(register_1_q), .b(2'b01), .eq(comparator_3_eq));  // open: gt, lt
  or or_1 (or_1_out, comparator_3_eq, comparator_4_eq);
  Comparator #(.width(2), .mode("unsigned")) comparator_4 (
    .a(register_1_q), .b(2'b10), .eq(comparator_4_eq));  // open: gt, lt
  Comparator #(.width(2), .mode("unsigned")) comparator_5 (
    .a(register_1_q), .b(2'b11), .eq(comparator_5_eq));  // open: gt, lt
  Multiplexer #(.width(2), .enable("false")) multiplexer_1 (
    .in0(2'b00), .in1(2'b01), .out(multiplexer_1_out), .sel(rts));
  Multiplexer #(.width(2), .enable("false")) multiplexer_2 (
    .in0(2'b10), .in1(2'b11), .out(multiplexer_2_out), .sel(comparator_1_eq));
  Multiplexer #(.width(2), .enable("false")) multiplexer_3 (
    .in0(2'b01), .in1(2'b11), .out(multiplexer_3_out), .sel(comparator_1_eq));
  Multiplexer #(.width(2), .enable("false")) multiplexer_4 (
    .in0(2'b00), .in1(2'b11), .out(multiplexer_4_out), .sel(stop));
  Multiplexer #(.width(19), .enable("false")) multiplexer_5 (
    .in0(register_2_q), .in1({1'b0, dout, parity_1_paritybit[1], 1'b1}), .out(multiplexer_5_out),
    .sel(and_1_out));
  Adder adder_1 (.a(register_3_q), .b(8'h1), .out(adder_1_out));  // open: cin, cout
  Multiplexer #(.select(2), .width(2), .enable("false")) multiplexer_6 (
    .in0(multiplexer_1_out), .in1(multiplexer_2_out), .in2(multiplexer_3_out), .in3(multiplexer_4_out),
    .out(multiplexer_6_out), .sel(register_1_q));
  Multiplexer #(.enable("false")) multiplexer_7 (
    .in0(1'b0), .in1(1'b1), .out(multiplexer_7_out), .sel(comparator_6_eq));
  Comparator #(.width(2), .mode("unsigned")) comparator_6 (
    .a(register_1_q), .b(2'b11), .eq(comparator_6_eq));  // open: gt, lt
  Multiplexer #(.width(19), .enable("false")) multiplexer_8 (
    .in0(multiplexer_5_out), .in1({register_2_q[17:0], 1'b1}), .out(multiplexer_8_out), .sel(or_1_out));
  Multiplexer #(.width(8), .enable("false")) multiplexer_9 (
    .in0(register_3_q), .in1(adder_1_out), .out(multiplexer_9_out), .sel(or_1_out));
  Multiplexer #(.width(8), .enable("false")) multiplexer_10 (
    .in0(multiplexer_9_out), .in1({8{1'b0}}), .out(multiplexer_10_out), .sel(and_1_out));
  Multiplexer #(.enable("false")) multiplexer_11 (
    .in0(d_ff_2_q), .in1(1'b0), .out(multiplexer_11_out), .sel(comparator_5_eq));
  Multiplexer #(.enable("false")) multiplexer_12 (
    .in0(multiplexer_11_out), .in1(1'b1), .out(multiplexer_12_out), .sel(and_1_out));
  Register #(.width(2)) register_1 (
    .D(multiplexer_6_out), .clk(baud_clock), .Q(register_1_q), .clr(reset));  // open: en
  D_Flip_Flop d_ff_1 (.D(multiplexer_7_out), .clk(baud_clock), .Q(sent_ok), .reset(reset));  // open: Qn, preset
  Register #(.width(19)) register_2 (
    .D(multiplexer_8_out), .clk(baud_clock), .Q(register_2_q), .clr(reset));  // open: en
  Register register_3 (.D(multiplexer_10_out), .clk(baud_clock), .Q(register_3_q), .clr(reset));  // open: en
  D_Flip_Flop d_ff_2 (.D(multiplexer_12_out), .clk(baud_clock), .Q(d_ff_2_q), .reset(reset));  // open: Qn, preset
  or or_2 (txbit, ~d_ff_2_q, register_2_q[18]);  // OR_Gate
  parity parity_1 (.indata(dout), .paritybit(parity_1_paritybit[1]));
endmodule

module recevive (
  input  stop,
  input  rx_bit,
  input  cts,
  input  baud_clock,
  input  reset,
  output clr_clk,
  output [17:0] din,
  output error,
  output done
);

  wire and_2_out, comparator_1_eq, comparator_2_eq, comparator_3_eq, comparator_4_eq, comparator_5_eq,
       multiplexer_9_out, or_1_out, parity_1_paritybit, xor_1_out;
  wire [1:0] multiplexer_1_out, multiplexer_2_out, multiplexer_3_out, multiplexer_4_out, multiplexer_6_out,
       register_1_q;
  wire [7:0] adder_1_out, multiplexer_5_out, multiplexer_7_out, register_2_q;
  wire [17:0] multiplexer_8_out;

  Comparator #(.width(2), .mode("unsigned")) comparator_1 (
    .a(register_1_q), .b(2'b00), .eq(comparator_1_eq));  // open: gt, lt
  Comparator #(.width(2), .mode("unsigned")) comparator_2 (
    .a(register_1_q), .b(2'b01), .eq(comparator_2_eq));  // open: gt, lt
  Comparator #(.width(2), .mode("unsigned")) comparator_3 (
    .a(register_1_q), .b(2'b10), .eq(comparator_3_eq));  // open: gt, lt
  Comparator #(.width(2), .mode("unsigned")) comparator_4 (
    .a(register_1_q), .b(2'b11), .eq(comparator_4_eq));  // open: gt, lt
  Comparator #(.mode("unsigned")) comparator_5 (.a(8'h11), .b(register_2_q), .eq(comparator_5_eq));  // open: gt, lt
  and and_1 (clr_clk, ~rx_bit, cts, comparator_1_eq);  // AND_Gate
  or or_1 (or_1_out, comparator_2_eq, comparator_3_eq);
  parity parity_1 (.indata(din[17:2]), .paritybit(parity_1_paritybit));
  Multiplexer #(.width(2), .enable("false")) multiplexer_1 (
    .in0(2'b00), .in1(2'b01), .out(multiplexer_1_out), .sel(clr_clk));
  Multiplexer #(.width(2), .enable("false")) multiplexer_2 (
    .in0(2'b10), .in1(2'b11), .out(multiplexer_2_out), .sel(comparator_5_eq));
  Multiplexer #(.width(2), .enable("false")) multiplexer_3 (
    .in0(2'b01), .in1(2'b11), .out(multiplexer_3_out), .sel(comparator_5_eq));
  Multiplexer #(.width(2), .enable("false")) multiplexer_4 (
    .in0(2'b00), .in1(2'b11), .out(multiplexer_4_out), .sel(stop));
  Multiplexer #(.width(8), .enable("false")) multiplexer_5 (
    .in0(register_2_q), .in1({8{1'b0}}), .out(multiplexer_5_out), .sel(clr_clk));
  xor xor_1 (xor_1_out, din[1], parity_1_paritybit);
  Multiplexer #(.select(2), .width(2), .enable("false")) multiplexer_6 (
    .in0(multiplexer_1_out), .in1(multiplexer_2_out), .in2(multiplexer_3_out), .in3(multiplexer_4_out),
    .out(multiplexer_6_out), .sel(register_1_q));
  Multiplexer #(.width(8), .enable("false")) multiplexer_7 (
    .in0(multiplexer_5_out), .in1(adder_1_out), .out(multiplexer_7_out), .sel(or_1_out));
  Adder adder_1 (.a(register_2_q), .b(8'h1), .out(adder_1_out));  // open: cin, cout
  Multiplexer #(.width(18), .enable("false")) multiplexer_8 (
    .in0(din), .in1({din[16:0], rx_bit}), .out(multiplexer_8_out), .sel(or_1_out));
  Multiplexer #(.enable("false")) multiplexer_9 (.in0(1'b0), .in1(1'b1), .out(multiplexer_9_out), .sel(and_2_out));
  and and_2 (and_2_out, comparator_4_eq, xor_1_out);
  Register #(.width(2)) register_1 (
    .D(multiplexer_6_out), .clk(baud_clock), .Q(register_1_q), .clr(reset));  // open: en
  Register register_2 (.D(multiplexer_7_out), .clk(baud_clock), .Q(register_2_q), .clr(reset));  // open: en
  Register #(.width(18)) register_3 (.D(multiplexer_8_out), .clk(baud_clock), .Q(din), .clr(reset));  // open: en
  D_Flip_Flop d_ff_1 (.D(multiplexer_9_out), .clk(baud_clock), .Q(error), .reset(reset));  // open: Qn, preset
  D_Flip_Flop d_ff_2 (.D(comparator_4_eq), .clk(baud_clock), .Q(done), .reset(reset));  // open: Qn, preset
endmodule

module parity (
  input  [15:0] indata,
  output paritybit
);

  ExactlyOne xor_1 (
    .out(paritybit), .in0(indata[0]), .in1(indata[1]), .in2(indata[2]), .in3(indata[3]), .in4(indata[4]),
    .in5(indata[5]), .in6(indata[6]), .in7(indata[7]), .in8(indata[8]), .in9(indata[9]), .in10(indata[10]),
    .in11(indata[11]), .in12(indata[12]), .in13(indata[13]), .in14(indata[14]), .in15(indata[15]));

  // Notes on the sheet:
  //   I6 BIT INPUT DATA
endmodule

module uart (
  input  [2:0] baudsel,
  input  clk,
  input  cycle,
  input  rxbit,
  input  cts,
  input  reset,
  input  rts,
  input  [15:0] dout,
  output [17:0] din,
  output error,
  output done,
  output done_2,
  output txbit
);

  wire baud_1_baud_clock, baud_2_baud_clock, recevive_1_clr_clk;

  baud baud_1 (.baud(baudsel), .clk(clk), .reset(reset), .clr_clk(recevive_1_clr_clk), .baud_clock(baud_1_baud_clock));
  recevive recevive_1 (
    .stop(cycle), .rx_bit(rxbit), .cts(cts), .baud_clock(baud_1_baud_clock), .reset(reset),
    .clr_clk(recevive_1_clr_clk), .din(din), .error(error), .done(done));
  baud baud_2 (.baud(baudsel), .clk(clk), .reset(reset), .clr_clk(1'b0), .baud_clock(baud_2_baud_clock));
  transmit transmit_1 (
    .rts(rts), .stop(cycle), .dout(dout), .reset(reset), .baud_clock(baud_2_baud_clock), .sent_ok(done_2),
    .txbit(txbit));
endmodule
